// Logisim project proyectoFinaVisualizacion.circ as structural Verilog: 1 circuit, main circuit main
module main (
);

  wire dipswitch_3_sw1, dipswitch_3_sw2, dipswitch_3_sw3, n7447_1_pin1, n7447_1_pin2, n7447_1_pin7,
       n7447_1_pin9, n7447_1_pin10, n7447_1_pin11, n7447_1_pin12, n7447_1_pin13, n7447_1_pin14,
       n7447_1_pin15, n7447_2_pin1, n7447_2_pin2, n7447_2_pin7, n7447_2_pin9, n7447_2_pin10, n7447_2_pin11,
       n7447_2_pin12, n7447_2_pin13, n7447_2_pin14, n7447_2_pin15, n7447_3_pin9, n7447_3_pin10,
       n7447_3_pin11, n7447_3_pin12, n7447_3_pin13, n7447_3_pin14, n7447_3_pin15;

  _7447 u_7447_1 (
    .pin1(n7447_1_pin1), .pin2(n7447_1_pin2), .pin7(n7447_1_pin7), .pin15(n7447_1_pin15),
    .pin14(n7447_1_pin14), .pin13(n7447_1_pin13), .pin12(n7447_1_pin12), .pin11(n7447_1_pin11),
    .pin10(n7447_1_pin10), .pin9(n7447_1_pin9));  // open: pin3, pin4, pin5, pin6
  _7_Segment_Display #(.active("false")) u_7_segment_display_1 (
    .g(n7447_1_pin14), .f(n7447_1_pin15), .a(n7447_1_pin13), .b(n7447_1_pin12), .e(n7447_1_pin9),
    .d(n7447_1_pin10), .c(n7447_1_pin11));  // open: dp
  DipSwitch #(.number(3)) dipswitch_1 (.sw1(n7447_1_pin2), .sw2(n7447_1_pin1), .sw3(n7447_1_pin7));
  _7_Segment_Display #(.active("false")) u_7_segment_display_2 (
    .g(n7447_2_pin14), .f(n7447_2_pin15), .a(n7447_2_pin13), .b(n7447_2_pin12), .e(n7447_2_pin9),
    .d(n7447_2_pin10), .c(n7447_2_pin11));  // open: dp
  _7447 u_7447_2 (
    .pin1(n7447_2_pin1), .pin2(n7447_2_pin2), .pin7(n7447_2_pin7), .pin15(n7447_2_pin15),
    .pin14(n7447_2_pin14), .pin13(n7447_2_pin13), .pin12(n7447_2_pin12), .pin11(n7447_2_pin11),
    .pin10(n7447_2_pin10), .pin9(n7447_2_pin9));  // open: pin3, pin4, pin5, pin6
  DipSwitch #(.number(3)) dipswitch_2 (.sw1(n7447_2_pin2), .sw2(n7447_2_pin1), .sw3(n7447_2_pin7));
  DipSwitch #(.number(3)) dipswitch_3 (.sw1(dipswitch_3_sw1), .sw2(dipswitch_3_sw2), .sw3(dipswitch_3_sw3));
  _7_Segment_Display #(.active("false")) u_7_segment_display_3 (
    .g(n7447_3_pin14), .f(n7447_3_pin15), .a(n7447_3_pin13), .b(n7447_3_pin12), .e(n7447_3_pin9),
    .d(n7447_3_pin10), .c(n7447_3_pin11));  // open: dp
  _7447 u_7447_3 (
    .pin1(dipswitch_3_sw2), .pin2(dipswitch_3_sw1), .pin7(dipswitch_3_sw3), .pin15(n7447_3_pin15),
    .pin14(n7447_3_pin14), .pin13(n7447_3_pin13), .pin12(n7447_3_pin12), .pin11(n7447_3_pin11),
    .pin10(n7447_3_pin10), .pin9(n7447_3_pin9));  // open: pin3, pin4, pin5, pin6
endmodule
