// Logisim project proyectoFinal.circ as structural Verilog: 2 circuits, main circuit main
module main (
);

  wire clock_1_out, dipswitch_3_sw1, dipswitch_3_sw2, dipswitch_4_sw5, dipswitch_4_sw6, dipswitch_4_sw7,
       dipswitch_4_sw8, dipswitch_5_sw1, dipswitch_5_sw2, j_k_ff_1_q, j_k_ff_1_qn, j_k_ff_2_q, j_k_ff_2_qn,
       j_k_ff_3_q, n7404_1_pin1, n7404_1_pin8, n7408_1_pin1, n7408_1_pin2, n7408_1_pin3, n7408_1_pin5,
       n7408_1_pin6, n7408_1_pin8, n7408_1_pin9, n7408_1_pin11, n7408_1_pin12, n7408_2_pin4, n7408_2_pin5,
       n7408_2_pin6, n7408_2_pin10, n7408_2_pin11, n7408_2_pin12, n7408_3_pin2, n7408_4_pin4, n7408_4_pin6,
       n7408_4_pin11, n7432_1_pin1, n7432_1_pin2, n7432_1_pin4, n7432_1_pin5, n7447_1_pin1, n7447_1_pin7,
       n7447_1_pin9, n7447_1_pin10, n7447_1_pin11, n7447_1_pin12, n7447_1_pin13, n7447_1_pin14,
       n7447_1_pin15, n7447_2_pin1, n7447_2_pin7, n7447_2_pin9, n7447_2_pin10, n7447_2_pin11, n7447_2_pin12,
       n7447_2_pin13, n7447_2_pin14, n7447_2_pin15, n7447_3_pin9, n7447_3_pin10, n7447_3_pin11,
       n7447_3_pin12, n7447_3_pin13, n7447_3_pin14, n7447_3_pin15, n7447_4_pin9, n7447_4_pin10,
       n7447_4_pin11, n7447_4_pin12, n7447_4_pin13, n7447_4_pin14, n7447_4_pin15, n7447_5_pin2, n7447_5_pin6,
       n7447_5_pin9, n7447_5_pin10, n7447_5_pin11, n7447_5_pin12, n7447_5_pin13, n7447_5_pin14,
       n7447_5_pin15, n7474_1_pin2, n7474_1_pin3, n7474_1_pin5, n7474_1_pin8, n7474_1_pin9, n7474_1_pin12,
       n747266_1_pin2, n747266_1_pin5, n747266_1_pin9, n747266_1_pin12;

  _7447 u_7447_1 (
    .pin1(n7447_1_pin1), .pin7(n7447_1_pin7), .pin15(n7447_1_pin15), .pin14(n7447_1_pin14),
    .pin13(n7447_1_pin13), .pin12(n7447_1_pin12), .pin11(n7447_1_pin11), .pin10(n7447_1_pin10),
    .pin9(n7447_1_pin9));  // open: pin2, pin3, pin4, pin5, pin6
  _7447 #(.ShowInternalStructure("true")) u_7447_2 (
    .pin1(n7447_2_pin1), .pin7(n7447_2_pin7), .pin15(n7447_2_pin15), .pin14(n7447_2_pin14),
    .pin13(n7447_2_pin13), .pin12(n7447_2_pin12), .pin11(n7447_2_pin11), .pin10(n7447_2_pin10),
    .pin9(n7447_2_pin9));  // open: pin2, pin3, pin4, pin5, pin6
  _7_Segment_Display #(.active("false")) u_7_segment_display_1 (
    .g(n7447_1_pin14), .f(n7447_1_pin15), .a(n7447_1_pin13), .b(n7447_1_pin12), .e(n7447_1_pin9),
    .d(n7447_1_pin10), .c(n7447_1_pin11));  // open: dp
  _7408 u_7408_1 (
    .pin1(n7408_1_pin1), .pin2(n7408_1_pin2), .pin3(n7408_1_pin3), .pin4(n7408_1_pin3), .pin5(n7408_1_pin5),
    .pin6(n7408_1_pin6), .pin13(n7408_1_pin6), .pin12(n7408_1_pin12), .pin11(n7408_1_pin11),
    .pin10(n7408_1_pin11), .pin9(n7408_1_pin9), .pin8(n7408_1_pin8));
  _7_Segment_Display #(.active("false")) u_7_segment_display_2 (
    .g(n7447_2_pin14), .f(n7447_2_pin15), .a(n7447_2_pin13), .b(n7447_2_pin12), .e(n7447_2_pin9),
    .d(n7447_2_pin10), .c(n7447_2_pin11));  // open: dp
  _747266 u_747266_1 (
    .pin1(n7447_1_pin1), .pin2(n747266_1_pin2), .pin3(n7408_1_pin1), .pin4(n7447_1_pin7),
    .pin5(n747266_1_pin5), .pin6(n7408_1_pin12), .pin13(n7447_2_pin1), .pin12(n747266_1_pin12),
    .pin11(n7408_1_pin2), .pin10(n7447_2_pin7), .pin9(n747266_1_pin9), .pin8(n7408_1_pin5));
  DipSwitch #(.number(2)) dipswitch_1 (.sw1(n7447_1_pin1), .sw2(n7447_1_pin7));
  DipSwitch #(.number(2)) dipswitch_2 (.sw1(n7447_2_pin1), .sw2(n7447_2_pin7));
  DipSwitch #(.number(2)) dipswitch_3 (.sw1(dipswitch_3_sw1), .sw2(dipswitch_3_sw2));
  DipSwitch dipswitch_4 (
    .sw1(n747266_1_pin2), .sw2(n747266_1_pin5), .sw3(n747266_1_pin12), .sw4(n747266_1_pin9),
    .sw5(dipswitch_4_sw5), .sw6(dipswitch_4_sw6), .sw7(dipswitch_4_sw7), .sw8(dipswitch_4_sw8));
  DipSwitch #(.number(2)) dipswitch_5 (.sw1(dipswitch_5_sw1), .sw2(dipswitch_5_sw2));
  _7_Segment_Display #(.active("false")) u_7_segment_display_3 (
    .g(n7447_3_pin14), .f(n7447_3_pin15), .a(n7447_3_pin13), .b(n7447_3_pin12), .e(n7447_3_pin9),
    .d(n7447_3_pin10), .c(n7447_3_pin11));  // open: dp
  _7408 u_7408_2 (
    .pin4(n7408_2_pin4), .pin5(n7408_2_pin5), .pin6(n7408_2_pin6), .pin13(n7408_1_pin8),
    .pin12(n7408_2_pin12), .pin11(n7408_2_pin11), .pin10(n7408_2_pin10), .pin9(n7408_2_pin11),
    .pin8(n7408_2_pin4));  // open: pin1, pin2, pin3
  _747266 u_747266_2 (
    .pin1(dipswitch_3_sw1), .pin2(dipswitch_4_sw5), .pin3(n7408_1_pin9), .pin4(dipswitch_3_sw2),
    .pin5(dipswitch_4_sw6), .pin6(n7408_2_pin5), .pin13(dipswitch_5_sw1), .pin12(dipswitch_4_sw7),
    .pin11(n7408_2_pin10), .pin10(dipswitch_5_sw2), .pin9(dipswitch_4_sw8), .pin8(n7408_2_pin12));
  _7447 #(.ShowInternalStructure("true")) u_7447_3 (
    .pin1(dipswitch_3_sw1), .pin7(dipswitch_3_sw2), .pin15(n7447_3_pin15), .pin14(n7447_3_pin14),
    .pin13(n7447_3_pin13), .pin12(n7447_3_pin12), .pin11(n7447_3_pin11), .pin10(n7447_3_pin10),
    .pin9(n7447_3_pin9));  // open: pin2, pin3, pin4, pin5, pin6
  _7447 #(.ShowInternalStructure("true")) u_7447_4 (
    .pin1(dipswitch_5_sw1), .pin7(dipswitch_5_sw2), .pin15(n7447_4_pin15), .pin14(n7447_4_pin14),
    .pin13(n7447_4_pin13), .pin12(n7447_4_pin12), .pin11(n7447_4_pin11), .pin10(n7447_4_pin10),
    .pin9(n7447_4_pin9));  // open: pin2, pin3, pin4, pin5, pin6
  _7_Segment_Display #(.active("false")) u_7_segment_display_4 (
    .g(n7447_4_pin14), .f(n7447_4_pin15), .a(n7447_4_pin13), .b(n7447_4_pin12), .e(n7447_4_pin9),
    .d(n7447_4_pin10), .c(n7447_4_pin11));  // open: dp
  _7404 #(.ShowInternalStructure("true")) u_7404_1 (
    .pin1(n7404_1_pin1), .pin9(n7408_2_pin6), .pin8(n7404_1_pin8));  // open: pin2, pin3, pin4, pin5, pin6, pin13, pin12, pin11, pin10
  LED led_1 (.in(n7474_1_pin12));
  LED led_2 (.in(n7474_1_pin2));
  _7474 #(.ShowInternalStructure("true")) u_7474_1 (
    .pin2(n7474_1_pin2), .pin3(n7474_1_pin3), .pin5(n7474_1_pin5), .pin6(n7474_1_pin2),
    .pin12(n7474_1_pin12), .pin11(n7474_1_pin3), .pin9(n7474_1_pin9), .pin8(n7474_1_pin8));  // open: pin1, pin4, pin13, pin10
  _7432 #(.ShowInternalStructure("true")) u_7432_1 (
    .pin1(n7432_1_pin1), .pin2(n7432_1_pin2), .pin3(n7474_1_pin12), .pin4(n7432_1_pin4), .pin5(n7432_1_pin5),
    .pin6(n7474_1_pin3));  // open: pin13, pin12, pin11, pin10, pin9, pin8
  _7408 #(.ShowInternalStructure("true")) u_7408_3 (
    .pin1(n7404_1_pin8), .pin2(n7408_3_pin2), .pin3(n7432_1_pin4), .pin4(n7474_1_pin2), .pin5(n7474_1_pin12),
    .pin6(n7432_1_pin5), .pin13(n7474_1_pin5), .pin12(n7474_1_pin8), .pin11(n7432_1_pin1),
    .pin10(n7474_1_pin2), .pin9(n7474_1_pin9), .pin8(n7432_1_pin2));
  Button button_1 (.out(n7408_3_pin2));
  J_K_Flip_Flop j_k_ff_1 (
    .J(n7474_1_pin3), .K(n7474_1_pin3), .clk(clock_1_out), .Q(j_k_ff_1_q), .Qn(j_k_ff_1_qn));  // open: preset, reset
  Clock clock_1 (.out(clock_1_out));
  J_K_Flip_Flop j_k_ff_2 (
    .J(n7474_1_pin3), .K(n7474_1_pin3), .clk(j_k_ff_1_q), .Q(j_k_ff_2_q), .Qn(j_k_ff_2_qn));  // open: preset, reset
  _7447 #(.ShowInternalStructure("true")) u_7447_5 (
    .pin1(j_k_ff_2_qn), .pin2(n7447_5_pin2), .pin6(n7447_5_pin6), .pin7(j_k_ff_1_qn), .pin15(n7447_5_pin15),
    .pin14(n7447_5_pin14), .pin13(n7447_5_pin13), .pin12(n7447_5_pin12), .pin11(n7447_5_pin11),
    .pin10(n7447_5_pin10), .pin9(n7447_5_pin9));  // open: pin3, pin4, pin5
  J_K_Flip_Flop j_k_ff_3 (
    .J(n7474_1_pin3), .K(n7474_1_pin3), .clk(j_k_ff_2_q), .Q(j_k_ff_3_q), .Qn(n7447_5_pin2));  // open: preset, reset
  J_K_Flip_Flop j_k_ff_4 (
    .J(n7474_1_pin3), .K(n7474_1_pin3), .clk(j_k_ff_3_q), .Qn(n7447_5_pin6));  // open: Q, preset, reset
  _7_Segment_Display #(.active("false")) u_7_segment_display_5 (
    .g(n7447_5_pin14), .f(n7447_5_pin15), .a(n7447_5_pin13), .b(n7447_5_pin12), .e(n7447_5_pin9),
    .d(n7447_5_pin10), .c(n7447_5_pin11));  // open: dp
  _7408 #(.ShowInternalStructure("true")) u_7408_4 (
    .pin4(n7408_4_pin4), .pin5(n7447_5_pin6), .pin6(n7408_4_pin6), .pin13(j_k_ff_1_qn), .pin12(j_k_ff_2_qn),
    .pin11(n7408_4_pin11), .pin10(n7408_4_pin11), .pin9(n7447_5_pin2), .pin8(n7408_4_pin4));  // open: pin1, pin2, pin3
endmodule

module advandage (
);

  wire and_1_out, and_2_out, and_3_out, and_4_out, and_5_out, and_6_out, and_7_out, undriven, undriven_2,
       undriven_3, undriven_4, undriven_5, undriven_6, undriven_7, undriven_8, undriven_9, undriven_10,
       undriven_11, undriven_12, undriven_13, undriven_14, undriven_15, undriven_16, xnor_1_out, xnor_2_out,
       xnor_3_out, xnor_4_out, xnor_5_out, xnor_6_out, xnor_7_out, xnor_8_out;

  xnor xnor_1 (xnor_1_out, undriven, undriven_9);
  xnor xnor_2 (xnor_2_out, undriven_2, undriven_10);
  xnor xnor_3 (xnor_3_out, undriven_3, undriven_11);
  xnor xnor_4 (xnor_4_out, undriven_4, undriven_12);
  xnor xnor_5 (xnor_5_out, undriven_5, undriven_13);
  xnor xnor_6 (xnor_6_out, undriven_6, undriven_14);
  xnor xnor_7 (xnor_7_out, undriven_7, undriven_15);
  xnor xnor_8 (xnor_8_out, undriven_8, undriven_16);
  and and_1 (and_1_out, xnor_1_out, xnor_2_out);
  and and_2 (and_2_out, xnor_3_out, xnor_4_out);
  and and_3 (and_3_out, xnor_5_out, xnor_6_out);
  and and_4 (and_4_out, xnor_7_out, xnor_8_out);
  and and_5 (and_5_out, and_1_out, and_2_out);
  and and_6 (and_6_out, and_3_out, and_4_out);
  and and_7 (and_7_out, and_5_out, and_6_out);
endmodule
