// Logisim project proyectoFinalCopy.circ as structural Verilog: 2 circuits, main circuit main
module main (
);

  wire and_1_out, clock_1_out, dipswitch_2_sw5, dipswitch_2_sw6, dipswitch_2_sw7, dipswitch_2_sw8,
       j_k_ff_1_q, j_k_ff_2_q, j_k_ff_3_q, j_k_ff_3_qn, j_k_ff_4_q, j_k_ff_4_qn, j_k_ff_5_q, n7408_1_pin1,
       n7408_1_pin2, n7408_1_pin3, n7408_1_pin5, n7408_1_pin6, n7408_1_pin8, n7408_1_pin9, n7408_1_pin11,
       n7408_1_pin12, n7408_2_pin4, n7408_2_pin5, n7408_2_pin6, n7408_2_pin10, n7408_2_pin11, n7408_2_pin12,
       n7408_3_pin1, n7408_3_pin2, n7408_3_pin3, n7408_3_pin5, n7408_3_pin6, n7408_3_pin11, n7408_3_pin12,
       n7408_3_pin13, n7408_4_pin4, n7408_4_pin6, n7408_4_pin11, n7447_1_pin9, n7447_1_pin10, n7447_1_pin11,
       n7447_1_pin12, n7447_1_pin13, n7447_1_pin14, n7447_1_pin15, n7447_2_pin2, n7447_2_pin6, n7447_2_pin9,
       n7447_2_pin10, n7447_2_pin11, n7447_2_pin12, n7447_2_pin13, n7447_2_pin14, n7447_2_pin15,
       n747266_1_pin2, n747266_1_pin5, n747266_1_pin9, n747266_1_pin12, or_1_out;
  wire [3:0] binary_to_bcd_converter_1_p2, binary_to_bcd_converter_1_p3, binary_to_bcd_converter_1_p4;
  wire [7:0] binary_to_bcd_converter_1_p1;

  Hex_Digit_Display hex_digit_display_1 (.value(binary_to_bcd_converter_1_p3));  // open: dp
  Hex_Digit_Display hex_digit_display_2 (.value(binary_to_bcd_converter_1_p2));  // open: dp
  // Binary_to_BCD_converter #(.binvalue(8)) binary_to_bcd_converter_1: pin names not known; wires that end beside it: binary_to_bcd_converter_1_p1, binary_to_bcd_converter_1_p2, binary_to_bcd_converter_1_p3, binary_to_bcd_converter_1_p4
  Hex_Digit_Display hex_digit_display_3 (.value(binary_to_bcd_converter_1_p4));  // open: dp
  _7408 u_7408_1 (
    .pin1(n7408_1_pin1), .pin2(n7408_1_pin2), .pin3(n7408_1_pin3), .pin4(n7408_1_pin3), .pin5(n7408_1_pin5),
    .pin6(n7408_1_pin6), .pin13(n7408_1_pin6), .pin12(n7408_1_pin12), .pin11(n7408_1_pin11),
    .pin10(n7408_1_pin11), .pin9(n7408_1_pin9), .pin8(n7408_1_pin8));
  _747266 #(.ShowInternalStructure("true")) u_747266_1 (
    .pin1(binary_to_bcd_converter_1_p1[7]), .pin2(n747266_1_pin2), .pin3(n7408_1_pin1),
    .pin4(binary_to_bcd_converter_1_p1[6]), .pin5(n747266_1_pin5), .pin6(n7408_1_pin12),
    .pin13(binary_to_bcd_converter_1_p1[5]), .pin12(n747266_1_pin12), .pin11(n7408_1_pin2),
    .pin10(binary_to_bcd_converter_1_p1[4]), .pin9(n747266_1_pin9), .pin8(n7408_1_pin5));
  DipSwitch dipswitch_1 (
    .sw1(binary_to_bcd_converter_1_p1[7]), .sw2(binary_to_bcd_converter_1_p1[6]),
    .sw3(binary_to_bcd_converter_1_p1[5]), .sw4(binary_to_bcd_converter_1_p1[4]),
    .sw5(binary_to_bcd_converter_1_p1[3]), .sw6(binary_to_bcd_converter_1_p1[2]),
    .sw7(binary_to_bcd_converter_1_p1[1]), .sw8(binary_to_bcd_converter_1_p1[0]));
  DipSwitch dipswitch_2 (
    .sw1(n747266_1_pin2), .sw2(n747266_1_pin5), .sw3(n747266_1_pin12), .sw4(n747266_1_pin9),
    .sw5(dipswitch_2_sw5), .sw6(dipswitch_2_sw6), .sw7(dipswitch_2_sw7), .sw8(dipswitch_2_sw8));
  _7408 #(.ShowInternalStructure("true")) u_7408_2 (
    .pin4(n7408_2_pin4), .pin5(n7408_2_pin5), .pin6(n7408_2_pin6), .pin13(n7408_1_pin8),
    .pin12(n7408_2_pin12), .pin11(n7408_2_pin11), .pin10(n7408_2_pin10), .pin9(n7408_2_pin11),
    .pin8(n7408_2_pin4));  // open: pin1, pin2, pin3
  _747266 u_747266_2 (
    .pin1(binary_to_bcd_converter_1_p1[3]), .pin2(dipswitch_2_sw5), .pin3(n7408_1_pin9),
    .pin4(binary_to_bcd_converter_1_p1[2]), .pin5(dipswitch_2_sw6), .pin6(n7408_2_pin5),
    .pin13(binary_to_bcd_converter_1_p1[1]), .pin12(dipswitch_2_sw7), .pin11(n7408_2_pin10),
    .pin10(binary_to_bcd_converter_1_p1[0]), .pin9(dipswitch_2_sw8), .pin8(n7408_2_pin12));
  _7408 #(.ShowInternalStructure("true")) u_7408_3 (
    .pin1(n7408_3_pin1), .pin2(n7408_3_pin2), .pin3(n7408_3_pin3), .pin4(n7408_3_pin3), .pin5(n7408_3_pin5),
    .pin6(n7408_3_pin6), .pin13(n7408_3_pin13), .pin12(n7408_3_pin12), .pin11(n7408_3_pin11));  // open: pin10, pin9, pin8
  _7404 #(.ShowInternalStructure("true")) u_7404_1 (
    .pin9(n7408_2_pin6), .pin8(n7408_3_pin1));  // open: pin1, pin2, pin3, pin4, pin5, pin6, pin13, pin12, pin11, pin10
  J_K_Flip_Flop j_k_ff_1 (
    .J(1'b1), .K(1'b1), .clk(n7408_3_pin6), .Q(j_k_ff_1_q), .Qn(n7408_3_pin13), .preset(or_1_out));  // open: reset
  _7447 #(.ShowInternalStructure("true")) u_7447_1 (
    .pin1(n7408_3_pin12), .pin7(n7408_3_pin13), .pin15(n7447_1_pin15), .pin14(n7447_1_pin14),
    .pin13(n7447_1_pin13), .pin12(n7447_1_pin12), .pin11(n7447_1_pin11), .pin10(n7447_1_pin10),
    .pin9(n7447_1_pin9));  // open: pin2, pin3, pin4, pin5, pin6
  J_K_Flip_Flop j_k_ff_2 (
    .J(1'b1), .K(1'b1), .clk(j_k_ff_1_q), .Q(j_k_ff_2_q), .Qn(n7408_3_pin12), .preset(or_1_out));  // open: reset
  _7432 #(.ShowInternalStructure("true")) u_7432_1 (
    .pin1(j_k_ff_2_q), .pin2(j_k_ff_1_q), .pin3(n7408_3_pin5));  // open: pin4, pin5, pin6, pin13, pin12, pin11, pin10, pin9, pin8
  Button button_1 (.out(n7408_3_pin2));
  _7_Segment_Display #(.active("false")) u_7_segment_display_1 (
    .g(n7447_1_pin14), .f(n7447_1_pin15), .a(n7447_1_pin13), .b(n7447_1_pin12), .e(n7447_1_pin9),
    .d(n7447_1_pin10), .c(n7447_1_pin11));  // open: dp
  J_K_Flip_Flop j_k_ff_3 (
    .J(n7408_3_pin11), .K(n7408_3_pin11), .clk(clock_1_out), .Q(j_k_ff_3_q), .Qn(j_k_ff_3_qn),
    .preset(n7408_4_pin6));  // open: reset
  Clock clock_1 (.out(clock_1_out));
  J_K_Flip_Flop j_k_ff_4 (
    .J(n7408_3_pin11), .K(n7408_3_pin11), .clk(j_k_ff_3_q), .Q(j_k_ff_4_q), .Qn(j_k_ff_4_qn),
    .preset(n7408_4_pin6));  // open: reset
  and and_1 (and_1_out, n7408_2_pin6, n7408_3_pin2, n7408_3_pin5);
  _7447 #(.ShowInternalStructure("true")) u_7447_2 (
    .pin1(j_k_ff_4_qn), .pin2(n7447_2_pin2), .pin6(n7447_2_pin6), .pin7(j_k_ff_3_qn), .pin15(n7447_2_pin15),
    .pin14(n7447_2_pin14), .pin13(n7447_2_pin13), .pin12(n7447_2_pin12), .pin11(n7447_2_pin11),
    .pin10(n7447_2_pin10), .pin9(n7447_2_pin9));  // open: pin3, pin4, pin5
  J_K_Flip_Flop j_k_ff_5 (
    .J(n7408_3_pin11), .K(n7408_3_pin11), .clk(j_k_ff_4_q), .Q(j_k_ff_5_q), .Qn(n7447_2_pin2),
    .preset(n7408_4_pin6));  // open: reset
  or or_1 (or_1_out, and_1_out, n7408_4_pin6);
  J_K_Flip_Flop j_k_ff_6 (
    .J(n7408_3_pin11), .K(n7408_3_pin11), .clk(j_k_ff_5_q), .Qn(n7447_2_pin6), .preset(n7408_4_pin6));  // open: Q, reset
  _7_Segment_Display #(.active("false")) u_7_segment_display_2 (
    .g(n7447_2_pin14), .f(n7447_2_pin15), .a(n7447_2_pin13), .b(n7447_2_pin12), .e(n7447_2_pin9),
    .d(n7447_2_pin10), .c(n7447_2_pin11));  // open: dp
  _7408 #(.ShowInternalStructure("true")) u_7408_4 (
    .pin4(n7408_4_pin4), .pin5(n7447_2_pin6), .pin6(n7408_4_pin6), .pin13(j_k_ff_3_qn), .pin12(j_k_ff_4_qn),
    .pin11(n7408_4_pin11), .pin10(n7408_4_pin11), .pin9(n7447_2_pin2), .pin8(n7408_4_pin4));  // open: pin1, pin2, pin3

  // Notes on the sheet:
  //   Entrada
  //   Contador de intentos
  //   Temporizador
endmodule

module advandage (
);

  wire and_1_out, and_2_out, and_3_out, and_4_out, and_5_out, and_6_out, and_7_out, undriven, undriven_2,
       undriven_3, undriven_4, undriven_5, undriven_6, undriven_7, undriven_8, undriven_9, undriven_10,
       undriven_11, undriven_12, undriven_13, undriven_14, undriven_15, undriven_16, xnor_1_out, xnor_2_out,
       xnor_3_out, xnor_4_out, xnor_5_out, xnor_6_out, xnor_7_out, xnor_8_out;

  xnor xnor_1 (xnor_1_out, undriven, undriven_9);
  xnor xnor_2 (xnor_2_out, undriven_2, undriven_10);
  xnor xnor_3 (xnor_3_out, undriven_3, undriven_11);
  xnor xnor_4 (xnor_4_out, undriven_4, undriven_12);
  xnor xnor_5 (xnor_5_out, undriven_5, undriven_13);
  xnor xnor_6 (xnor_6_out, undriven_6, undriven_14);
  xnor xnor_7 (xnor_7_out, undriven_7, undriven_15);
  xnor xnor_8 (xnor_8_out, undriven_8, undriven_16);
  and and_1 (and_1_out, xnor_1_out, xnor_2_out);
  and and_2 (and_2_out, xnor_3_out, xnor_4_out);
  and and_3 (and_3_out, xnor_5_out, xnor_6_out);
  and and_4 (and_4_out, xnor_7_out, xnor_8_out);
  and and_5 (and_5_out, and_1_out, and_2_out);
  and and_6 (and_6_out, and_3_out, and_4_out);
  and and_7 (and_7_out, and_5_out, and_6_out);
endmodule
